// Logisim project flip_flop.circ as structural Verilog: 1 circuit, main circuit main
module main (
  input  SET,
  input  RESET,
  output OUTPUT
);

  wire and_1_out, not_1_out;

  not not_1 (not_1_out, RESET);
  and and_1 (and_1_out, not_1_out, OUTPUT);
  or or_1 (OUTPUT, SET, and_1_out);
endmodule
