// Logisim project toplama_devresi.circ as structural Verilog: 1 circuit, main circuit main
module main (
  input  in_1,
  input  in_2,
  output TOPLAM,
  output ELDE
);

  xor xor_1 (TOPLAM, in_1, in_2);
  and and_1 (ELDE, in_2, in_1);

  // Notes on the sheet:
  //   TOPLAMA DEVRESİ
endmodule
